# Fritzing sketch 00_TX_RC_ESPNOW_CARS_ESP8266 (saved by Fritzing 0.9.10b)

parts:
  Componente1 = Thumb Joystick
  Bat1 = battery_holder_dual_18650 [part_number=TBH-18650-2A-P]
  IC1 = Voltage Regulator [package=78xxl]
  S5 = Pushbutton [package="[SMD]"]
  R1 = Resistor [tolerance=±5% power=0.25 resistance=10k package=THT]
  R2 = Resistor [tolerance=±5% power=0.25 resistance=10k package=THT]
  S1 = Pushbutton [package="[SMD]"]
  S4 = Pushbutton [package="[SMD]"]
  S2 = Pushbutton [package="[SMD]"]
  S3 = Pushbutton [package="[SMD]"]
  U4 = NodeMCU V1.0

nets:
  GND: Componente1.GND, Bat1.+#2, IC1.GND, R1.Pin_0, R2.Pin_1, U4.GND
  N1: Componente1.SEL, U4.D2
  N2: Componente1.HORZ, U4.D1
  N3: Componente1.VERT, U4.D0
  VCC: Componente1.VCC, U4.3V3
  N4: Bat1.+#1, IC1.IN
  N5: IC1.OUT, U4.Vin
  N6: S5.Pin_1, S5.Pin_2, U4.D3
  N7: S5.Pin_3, S5.Pin_4, R1.Pin_1
  N8: R2.Pin_0, S1.Pin_3, S1.Pin_4, S4.Pin_3, S4.Pin_4, S2.Pin_3, S2.Pin_4, S3.Pin_3, S3.Pin_4
  N9: S1.Pin_1, S1.Pin_2, U4.D4
  N10: S4.Pin_1, S4.Pin_2, U4.D6
  N11: S2.Pin_1, S2.Pin_2, U4.D5
  N12: S3.Pin_1, U4.D7

notes:
  7.4v 2s Cells
  Joystick
  7805
  LREAR
  LFRONT
  LPLEFT
  Lights button or switch
  HORN
  LPRIGHT
  ESP8266

custom parts:
  battery_holder_dual_18650: TBH-18650-2A-P dual 18650 battery holder.
  NodeMCU V1.0: ESP8266 based NodeMCU
